# Fritzing sketch 1D-Pong (saved by Fritzing 1.0.2b)
perfboards: 1

parts:
  Part1 = Arduino Nano (Rev3.0)
  Button_A = male pin header, 4 pins [form="♂ (male)"]
  Button_B = male pin header, 4 pins [form="♂ (male)"]
  Power = female pin header, 2 pins [form="♀ (female)"]
  Q1 = NPN-Transistor [package="TO92 [THT]"]
  R1 = Resistor [tolerance=±1% resistance=1k package="0805 [SMD]"]
  Q2 = NPN-Transistor [package="TO92 [THT]"]
  R2 = Resistor [tolerance=±1% resistance=1k package="0805 [SMD]"]
  Button_Bright = male pin header, 2 pins [form="♂ (male)"]
  R3 = Resistor [tolerance=±1% resistance=47 package="0805 [SMD]"]
  LED_Strip = male pin header, 3 pins [form="♂ (male)"]

nets:
  GND: Part1.GND, Button_A.pin2, Button_B.pin2, Power.pin2, Q1.E, Q2.E, Button_Bright.pin2, LED_Strip.pin2
  N1: Part1.D2, R3.Pin_0
  N2: Part1.D3, Button_A.pin3
  N3: Part1.D4, R1.Pin_0
  N4: Part1.D5, Button_B.pin3
  N5: Part1.D6, R2.Pin_0
  N6: Part1.D7, Button_Bright.pin1
  12V: Part1.VIN, Button_A.pin1, Button_B.pin1, Power.pin1, LED_Strip.pin1
  N7: Button_A.pin4, Q1.C
  N8: Button_B.pin4, Q2.C
  N9: Q1.B, R1.Pin_1
  N10: Q2.B, R2.Pin_1
  N11: R3.Pin_1, LED_Strip.pin3
